// Logisim project Lab2OrderingMachine.circ as structural Verilog: 1 circuit, main circuit main
module main (
  input  [2:0] User,
  output Kitchen0,
  output Kitchen1,
  output Kitchen2,
  output Kitchen3,
  output Kitchen4,
  output Kitchen5,
  output Kitchen6,
  output Kitchen7
);

  wire decoder_1_out0, decoder_1_out1, decoder_1_out2, decoder_1_out3, not_1_out;

  Decoder #(.select(2)) decoder_1 (
    .out0(decoder_1_out0), .out1(decoder_1_out1), .out2(decoder_1_out2), .out3(decoder_1_out3),
    .sel(User[1:0]));  // open: en
  not not_1 (not_1_out, User[2]);
  and and_1 (Kitchen0, not_1_out, decoder_1_out0);
  and and_2 (Kitchen1, not_1_out, decoder_1_out1);
  and and_3 (Kitchen2, not_1_out, decoder_1_out2);
  and and_4 (Kitchen3, not_1_out, decoder_1_out3);
  and and_5 (Kitchen4, decoder_1_out0, User[2]);
  and and_6 (Kitchen5, decoder_1_out1, User[2]);
  and and_7 (Kitchen6, decoder_1_out2, User[2]);
  and and_8 (Kitchen7, decoder_1_out3, User[2]);
endmodule
