// Logisim project Lab2OrderingMachine_Availability.circ as structural Verilog: 1 circuit, main circuit main
module main (
  input  [2:0] User,
  input  [7:0] Inventory,
  output Kitchen0,
  output Kitchen1,
  output Kitchen2,
  output Kitchen3,
  output Kitchen4,
  output Kitchen5,
  output Kitchen6,
  output Kitchen7
);

  wire and_1_out, and_2_out, and_3_out, and_4_out, and_5_out, and_6_out, and_7_out, and_8_out,
       decoder_1_out0, decoder_1_out1, decoder_1_out2, decoder_1_out3, multiplexer_1_out, not_1_out;
  wire [2:0] priority_encoder_1_out;

  Decoder #(.select(2)) decoder_1 (
    .out0(decoder_1_out0), .out1(decoder_1_out1), .out2(decoder_1_out2), .out3(decoder_1_out3),
    .sel(User[1:0]));  // open: en
  Priority_Encoder priority_encoder_1 (
    .in0(Inventory[0]), .in1(Inventory[1]), .in2(Inventory[2]), .in3(Inventory[3]), .in4(Inventory[4]),
    .in5(Inventory[5]), .in6(Inventory[6]), .in7(Inventory[7]), .out(priority_encoder_1_out));  // open: en_in, gs, en_out
  not not_1 (not_1_out, User[2]);
  and and_1 (and_1_out, not_1_out, decoder_1_out0);
  and and_2 (and_2_out, not_1_out, decoder_1_out1);
  and and_3 (and_3_out, not_1_out, decoder_1_out2);
  and and_4 (and_4_out, not_1_out, decoder_1_out3);
  and and_5 (and_5_out, decoder_1_out0, User[2]);
  and and_6 (and_6_out, decoder_1_out1, User[2]);
  and and_7 (and_7_out, decoder_1_out2, User[2]);
  and and_8 (and_8_out, decoder_1_out3, User[2]);
  Multiplexer #(.select(3)) multiplexer_1 (
    .in0(and_1_out), .in1(and_2_out), .in2(and_3_out), .in3(and_4_out), .in4(and_5_out), .in5(and_6_out),
    .in6(and_7_out), .in7(and_8_out), .out(multiplexer_1_out), .sel(priority_encoder_1_out));
  and and_9 (Kitchen0, and_1_out, multiplexer_1_out);
  and and_10 (Kitchen1, and_2_out, multiplexer_1_out);
  and and_11 (Kitchen2, and_3_out, multiplexer_1_out);
  and and_12 (Kitchen3, and_4_out, multiplexer_1_out);
  and and_13 (Kitchen4, and_5_out, multiplexer_1_out);
  and and_14 (Kitchen5, and_6_out, multiplexer_1_out);
  and and_15 (Kitchen6, and_7_out, and_7_out);
  and and_16 (Kitchen7, and_8_out, and_8_out);
endmodule
