// Logisim project Lab2OrderingMachine_Availability_WithPayment.circ as structural Verilog: 1 circuit, main circuit main
module main (
  input  [2:0] x,
  input  [7:0] Inventory,
  input  [7:0] Payment,
  output Kitchen0,
  output Kitchen1,
  output Kitchen2,
  output Kitchen3,
  output Kitchen4,
  output Kitchen5,
  output Kitchen6,
  output Kitchen7,
  output [7:0] A,
  output [2:0] out_13
);

  wire and_1_out, and_2_out, and_3_out, and_4_out, and_5_out, and_6_out, and_7_out, and_8_out,
       comparator_1_eq, comparator_1_gt, decoder_1_out0, decoder_1_out1, decoder_1_out2, decoder_1_out3,
       nor_1_out, nor_3_out, nor_4_out, nor_5_out, not_1_out, not_2_out, not_3_out, not_4_out, not_5_out,
       not_6_out, not_7_out, not_8_out, or_1_out;

  Decoder #(.select(2)) decoder_1 (
    .out0(decoder_1_out0), .out1(decoder_1_out1), .out2(decoder_1_out2), .out3(decoder_1_out3), .sel(x[1:0]));  // open: en
  not not_1 (not_1_out, x[2]);
  not not_2 (not_2_out, Inventory[0]);
  not not_3 (not_3_out, Inventory[1]);
  not not_4 (not_4_out, Inventory[2]);
  not not_5 (not_5_out, Inventory[3]);
  not not_6 (not_6_out, Inventory[4]);
  not not_7 (not_7_out, Inventory[5]);
  not not_8 (not_8_out, Inventory[7]);
  Priority_Encoder priority_encoder_1 (
    .in0(Payment[0]), .in1(Payment[1]), .in2(Payment[2]), .in3(Payment[3]), .in4(Payment[4]),
    .in5(Payment[5]), .in6(Payment[6]), .in7(Payment[7]), .out(out_13));  // open: en_in, gs, en_out
  nor nor_1 (nor_1_out, Inventory[1], Inventory[2]);
  and and_1 (and_1_out, not_1_out, decoder_1_out0);
  and and_2 (and_2_out, not_1_out, decoder_1_out1);
  and and_3 (and_3_out, not_1_out, decoder_1_out2);
  and and_4 (and_4_out, not_1_out, decoder_1_out3);
  and and_5 (and_5_out, decoder_1_out0, x[2]);
  and and_6 (and_6_out, decoder_1_out1, x[2]);
  and and_7 (and_7_out, decoder_1_out2, x[2]);
  and and_8 (and_8_out, decoder_1_out3, x[2]);
  nor nor_2 (A[0], not_2_out, nor_1_out);
  nor nor_3 (nor_3_out, Inventory[0], Inventory[3]);
  nor nor_4 (nor_4_out, Inventory[1], Inventory[3]);
  nor nor_5 (nor_5_out, Inventory[2], Inventory[6]);
  nor nor_6 (A[1], nor_4_out, nor_4_out);
  Comparator #(.mode("unsigned"), .width(3)) comparator_1 (
    .a(out_13), .b(x), .gt(comparator_1_gt), .eq(comparator_1_eq));  // open: lt
  nor nor_7 (A[2], nor_3_out, nor_5_out);
  nor nor_8 (A[3], not_2_out, not_5_out, not_4_out);
  nor nor_9 (A[4], not_2_out, not_3_out);
  nor nor_10 (A[5], not_2_out, not_5_out, not_8_out);
  nor nor_11 (A[6], not_6_out, not_8_out);
  nor nor_12 (A[7], not_6_out, not_7_out);
  or or_1 (or_1_out, comparator_1_gt, comparator_1_eq);
  and and_9 (Kitchen0, and_1_out, or_1_out, A[0]);
  and and_10 (Kitchen1, and_2_out, or_1_out, A[1]);
  and and_11 (Kitchen2, and_3_out, or_1_out, A[2]);
  and and_12 (Kitchen3, and_4_out, or_1_out, A[3]);
  and and_13 (Kitchen4, and_5_out, or_1_out, A[4]);
  and and_14 (Kitchen5, and_6_out, or_1_out, A[5]);
  and and_15 (Kitchen6, and_7_out, or_1_out, A[6]);
  and and_16 (Kitchen7, and_8_out, or_1_out, A[7]);
endmodule
