// Logisim project ECEProject_3_MomentumSelectorSolution.circ as structural Verilog: 1 circuit, main circuit main
module main (
  input  [7:0] S,
  input  [7:0] T,
  output S_more_T,
  output Trigger,
  output S_equal_T,
  output S_less_T
);

  wire and_1_out, and_2_out, and_3_out, comparator_1_eq, comparator_1_gt, not_1_out, not_2_out, xnor_1_out;
  wire [2:0] priority_encoder_1_out, priority_encoder_2_out;

  Priority_Encoder priority_encoder_1 (
    .in0(S[0]), .in1(S[1]), .in2(S[2]), .in3(S[3]), .in4(S[4]), .in5(S[5]), .in6(S[6]), .in7(S[7]),
    .out(priority_encoder_1_out));  // open: en_in, gs, en_out
  Priority_Encoder priority_encoder_2 (
    .in0(T[0]), .in1(T[1]), .in2(T[2]), .in3(T[3]), .in4(T[4]), .in5(T[5]), .in6(T[6]), .in7(T[7]),
    .out(priority_encoder_2_out));  // open: en_in, gs, en_out
  Comparator #(.mode("unsigned"), .width(2)) comparator_1 (
    .a(priority_encoder_1_out[2:1]), .b(priority_encoder_2_out[2:1]), .gt(comparator_1_gt),
    .eq(comparator_1_eq));  // open: lt
  not not_1 (not_1_out, priority_encoder_2_out[0]);
  not not_2 (not_2_out, priority_encoder_1_out[0]);
  and and_1 (and_1_out, priority_encoder_1_out[0], not_1_out);
  xnor xnor_1 (xnor_1_out, priority_encoder_1_out[0], priority_encoder_2_out[0]);
  and and_2 (and_2_out, not_2_out, priority_encoder_2_out[0]);
  and and_3 (and_3_out, comparator_1_eq, and_1_out);
  or or_1 (S_more_T, comparator_1_gt, and_3_out);
  and and_4 (S_equal_T, comparator_1_eq, xnor_1_out);
  and and_5 (S_less_T, comparator_1_eq, and_2_out);
  or or_2 (Trigger, S_more_T, S_equal_T);
endmodule
