// Logisim project ECE_Project_3_ParticleFlaggerSolution.circ as structural Verilog: 1 circuit, main circuit main
module main (
  input  [5:0] C,
  input  [5:0] Q,
  output Trigger_2
);

  wire decoder_1_out0, decoder_1_out1, decoder_1_out2, decoder_1_out3, decoder_1_out4, decoder_1_out5,
       decoder_1_out6, decoder_1_out7, decoder_2_out0, decoder_2_out1, decoder_2_out2, decoder_2_out3,
       decoder_2_out4, decoder_2_out5, decoder_2_out6, decoder_2_out7, multiplexer_1_out, multiplexer_2_out;

  Decoder #(.select(3)) decoder_1 (
    .out0(decoder_1_out0), .out1(decoder_1_out1), .out2(decoder_1_out2), .out3(decoder_1_out3),
    .out4(decoder_1_out4), .out5(decoder_1_out5), .out6(decoder_1_out6), .out7(decoder_1_out7),
    .sel({C[4], C[2], C[0]}));  // open: en
  Decoder #(.select(3)) decoder_2 (
    .out0(decoder_2_out0), .out1(decoder_2_out1), .out2(decoder_2_out2), .out3(decoder_2_out3),
    .out4(decoder_2_out4), .out5(decoder_2_out5), .out6(decoder_2_out6), .out7(decoder_2_out7),
    .sel({C[5], C[3], C[1]}));  // open: en
  Multiplexer #(.select(3)) multiplexer_1 (
    .in0(decoder_1_out0), .in1(decoder_1_out1), .in2(decoder_1_out2), .in3(decoder_1_out3),
    .in4(decoder_1_out4), .in5(decoder_1_out5), .in6(decoder_1_out6), .in7(decoder_1_out7),
    .out(multiplexer_1_out), .sel({Q[4], Q[2], Q[0]}));
  Multiplexer #(.select(3)) multiplexer_2 (
    .in0(decoder_2_out0), .in1(decoder_2_out1), .in2(decoder_2_out2), .in3(decoder_2_out3),
    .in4(decoder_2_out4), .in5(decoder_2_out5), .in6(decoder_2_out6), .in7(decoder_2_out7),
    .out(multiplexer_2_out), .sel({Q[5], Q[3], Q[1]}));
  and and_1 (Trigger_2, multiplexer_1_out, multiplexer_2_out);
endmodule
