// Logisim project ECE_Project_1_L.circ as structural Verilog: 1 circuit, main circuit main
module main (
  input  x,
  input  y,
  input  z,
  output L
);

  wire not_1_out, not_2_out, not_3_out, or_1_out, or_2_out, or_3_out;

  not not_1 (not_1_out, x);
  not not_2 (not_2_out, y);
  not not_3 (not_3_out, z);
  or or_1 (or_1_out, not_1_out, not_2_out);
  or or_2 (or_2_out, not_1_out, not_3_out);
  or or_3 (or_3_out, not_2_out, not_3_out);
  and and_1 (L, or_1_out, or_2_out, or_3_out);
endmodule
