// Logisim project ECE_Project_1_Part1BSolution.circ as structural Verilog: 1 circuit, main circuit main
module main (
  input  x,
  input  y,
  output f,
  output g,
  output f2,
  output g2
);

  wire and_1_out, and_2_out, nand_1_out, nand_2_out, nand_3_out, nor_1_out, nor_2_out, nor_3_out, not_1_out,
       not_2_out, or_1_out, or_2_out;

  not not_1 (not_1_out, x);
  not not_2 (not_2_out, y);
  and and_1 (and_1_out, not_1_out, y);
  and and_2 (and_2_out, x, not_2_out);
  or or_1 (or_1_out, not_2_out, not_1_out);
  or or_2 (or_2_out, y, x);
  nor nor_1 (nor_1_out, x, not_2_out);
  nor nor_2 (nor_2_out, not_1_out, y);
  nand nand_1 (nand_1_out, x, y);
  nand nand_2 (nand_2_out, not_2_out, not_1_out);
  nand nand_3 (nand_3_out, nand_1_out, nand_2_out);
  or or_3 (f, and_1_out, and_2_out);
  and and_3 (g, or_1_out, or_2_out);
  nor nor_3 (nor_3_out, nor_1_out, nor_2_out);
  nor nor_4 (f2, nor_3_out, nor_3_out);
  nand nand_4 (g2, nand_3_out, nand_3_out);
endmodule
