// Logisim project ECE_Project_1_Part1Solution.circ as structural Verilog: 1 circuit, main circuit main
module main (
  input  x,
  input  y,
  output f,
  output g
);

  wire and_1_out, and_2_out, not_1_out, not_2_out, or_1_out, or_2_out;

  not not_1 (not_1_out, x);
  not not_2 (not_2_out, y);
  and and_1 (and_1_out, not_1_out, y);
  and and_2 (and_2_out, x, not_2_out);
  or or_1 (or_1_out, not_2_out, not_1_out);
  or or_2 (or_2_out, y, x);
  or or_3 (f, and_1_out, and_2_out);
  and and_3 (g, or_1_out, or_2_out);
endmodule
