// Logisim project ECE_Project_1_Part3Comparison.circ as structural Verilog: 1 circuit, main circuit main
module main (
  input  x,
  input  y,
  input  z,
  output H1,
  output H2
);

  wire and_1_out, and_2_out, and_3_out, not_1_out, not_2_out, not_3_out, or_1_out;

  not not_1 (not_1_out, x);
  not not_2 (not_2_out, y);
  not not_3 (not_3_out, z);
  and and_1 (and_1_out, not_3_out, y);
  and and_2 (and_2_out, z, not_2_out);
  or or_1 (or_1_out, and_1_out, and_2_out);
  and and_3 (and_3_out, not_1_out, or_1_out);
  or or_2 (H1, x, and_3_out);
  or or_3 (H2, x, or_1_out);
endmodule
