// Logisim project ECE_Project_5_BarcodeScannerSolution.circ as structural Verilog: 1 circuit, main circuit main
module main (
  input  x,
  input  Clock,
  output y_1_new,
  output z,
  output y_2_new
);

  wire d_ff_1_q, d_ff_2_q, nand_1_out, nand_2_out, nand_3_out, nand_4_out, nand_5_out, nand_6_out,
       nand_7_out, nand_8_out, nand_9_out, nand_10_out, nand_11_out, nand_13_out, nand_14_out, nand_16_out;

  nand nand_1 (nand_1_out, x, x);
  nand nand_2 (nand_2_out, d_ff_1_q, d_ff_1_q);
  nand nand_3 (nand_3_out, d_ff_2_q, d_ff_2_q);
  nand nand_4 (nand_4_out, x, d_ff_1_q);
  D_Flip_Flop d_ff_1 (.D(y_1_new), .clk(Clock), .Q(d_ff_1_q));  // open: Qn, preset, reset
  D_Flip_Flop d_ff_2 (.D(y_2_new), .clk(Clock), .Q(d_ff_2_q));  // open: Qn, preset, reset
  nand nand_5 (nand_5_out, nand_4_out, nand_4_out);
  nand nand_6 (nand_6_out, nand_1_out, nand_2_out);
  nand nand_7 (nand_7_out, x, d_ff_1_q);
  nand nand_8 (nand_8_out, nand_3_out, nand_5_out);
  nand nand_9 (nand_9_out, nand_2_out, x);
  nand nand_10 (nand_10_out, nand_6_out, nand_6_out);
  nand nand_11 (nand_11_out, nand_7_out, nand_7_out);
  nand nand_12 (y_2_new, nand_8_out, nand_9_out);
  nand nand_13 (nand_13_out, nand_10_out, d_ff_2_q);
  nand nand_14 (nand_14_out, nand_11_out, nand_3_out);
  nand nand_15 (y_1_new, nand_13_out, nand_14_out);
  nand nand_16 (nand_16_out, y_1_new, y_2_new);
  nand nand_17 (z, nand_16_out, nand_16_out);
endmodule
