// Logisim project ECE_Project_5_RateCalculatorSolution.circ as structural Verilog: 1 circuit, main circuit main
module main (
  input  x,
  input  reset_button,
  output [2:0] z,
  output [2:0] Y
);

  wire [2:0] bit_extender_1_out;

  assign bit_extender_1_out = {{2{1'b0}}, x};  // Bit_Extender bit_extender_1
  Adder #(.width(3)) adder_1 (.a(bit_extender_1_out), .b(Y), .out(z));  // open: cin, cout
  D_Flip_Flop #(.trigger("falling")) D_0 (.D(z[0]), .clk(x), .Q(Y[0]), .reset(reset_button));  // open: Qn, preset
  D_Flip_Flop #(.trigger("falling")) D_1 (.D(z[1]), .clk(x), .Q(Y[1]), .reset(reset_button));  // open: Qn, preset
  D_Flip_Flop #(.trigger("falling")) D_2 (.D(z[2]), .clk(x), .Q(Y[2]), .reset(reset_button));  // open: Qn, preset
endmodule
