// Logisim project Lab4HazardBSM_QuickFix.circ as structural Verilog: 1 circuit, main circuit main
module main (
  input  C3,
  input  C2,
  input  C1,
  input  C0,
  output S
);

  wire not_1_out, not_2_out, not_3_out, not_4_out, or_1_out, or_2_out, or_3_out, S1_out, S2_out, S3_out,
       S4_out;

  not not_1 (not_1_out, C3);
  not not_2 (not_2_out, C2);
  not not_3 (not_3_out, C1);
  not not_4 (not_4_out, C0);
  or or_1 (or_1_out, C1, C1);
  or or_2 (or_2_out, C3, C3);
  or or_3 (or_3_out, C1, C1);
  or S1 (S1_out, or_2_out, or_3_out);
  or S2 (S2_out, not_1_out, not_4_out);
  or S3 (S3_out, not_1_out, not_2_out, not_3_out);
  or S4 (S4_out, not_2_out, or_1_out, not_4_out);
  and and_1 (S, S1_out, S2_out, S3_out, S4_out);
endmodule
