// Logisim project Lab4HazardDWM_QuickFix.circ as structural Verilog: 1 circuit, main circuit main
module main (
  input  D3,
  input  D2,
  input  D1,
  input  D0,
  output F
);

  wire F1_out, F2_out, F3_out, F4_out, not_1_out, not_2_out, or_1_out, or_2_out, or_3_out, or_4_out;

  or or_1 (or_1_out, D3, D3);
  not not_1 (not_1_out, D3);
  not not_2 (not_2_out, D2);
  or or_2 (or_2_out, D1, D1);
  or or_3 (or_3_out, D2, D2);
  or or_4 (or_4_out, D0, D0);
  and F1 (F1_out, not_1_out, not_2_out, or_4_out);
  and F2 (F2_out, or_1_out, or_3_out, or_2_out);
  and F3 (F3_out, not_1_out, or_3_out, or_2_out, or_4_out);
  and F4 (F4_out, or_2_out, or_4_out, or_1_out, not_2_out);
  or or_5 (F, F1_out, F2_out, F3_out, F4_out);
endmodule
