// Logisim project Lab4HazardFreeDWM.circ as structural Verilog: 1 circuit, main circuit main
module main (
  input  D3,
  input  D2,
  input  D1,
  input  D0,
  output F
);

  wire F1_out, F2_out, F3_out, F4_out, F_c_out, not_1_out, not_2_out;

  not not_1 (not_1_out, D3);
  not not_2 (not_2_out, D2);
  and F1 (F1_out, not_1_out, not_2_out, D0);
  and F2 (F2_out, D3, D2, D1);
  and F3 (F3_out, not_1_out, D2, D1, D0);
  and F4 (F4_out, D1, D0, D3, not_2_out);
  and F_c (F_c_out, D0, D1);
  or or_1 (F, F1_out, F2_out, F_c_out, F3_out, F4_out);
endmodule
