// Logisim project ECE_Project_4_BSMOld.circ as structural Verilog: 1 circuit, main circuit main
module main (
  input  C_3,
  input  C_2,
  input  C_1,
  input  C_0,
  output S
);

  wire nor_1_out, nor_2_out, nor_3_out, nor_4_out, nor_5_out, nor_6_out;

  nor nor_1 (nor_1_out, C_3, C_3);
  nor nor_2 (nor_2_out, C_3, C_2);
  nor nor_3 (nor_3_out, nor_1_out, C_1);
  nor nor_4 (nor_4_out, C_2, C_0);
  nor nor_5 (nor_5_out, nor_2_out, nor_3_out);
  nor nor_6 (nor_6_out, nor_5_out, nor_5_out);
  nor nor_7 (S, nor_6_out, nor_4_out);
endmodule
