// Logisim project ECE_Project_4_BSM_HazardAndConsensus.circ as structural Verilog: 1 circuit, main circuit main
module main (
  input  C_3,
  input  C_2,
  input  C_1,
  input  C_0,
  output S
);

  wire Consensus_out, not_1_out, or_1_out, or_2_out, or_3_out;

  or or_1 (or_1_out, C_3, C_2);
  not not_1 (not_1_out, C_3);
  or or_2 (or_2_out, not_1_out, C_1);
  or Consensus (Consensus_out, C_1, C_2);
  or or_3 (or_3_out, C_2, C_0);
  and and_1 (S, or_1_out, or_3_out, Consensus_out, or_2_out);
endmodule
