// Logisim project ECE_Project_4_DWM_Consensus.circ as structural Verilog: 1 circuit, main circuit main
module main (
  input  D_3,
  input  D_2,
  input  D_1,
  input  D_0,
  output F
);

  wire and_1_out, and_2_out, and_3_out, C_1_out, C_2_out, C_3_out, not_1_out, not_2_out, not_3_out;

  not not_1 (not_1_out, D_2);
  not not_2 (not_2_out, D_1);
  not not_3 (not_3_out, D_0);
  and and_1 (and_1_out, not_1_out, not_3_out);
  and and_2 (and_2_out, D_3, D_2, not_2_out);
  and and_3 (and_3_out, D_3, D_1, D_0);
  and C_1 (C_1_out, D_3, D_2, D_0);
  and C_2 (C_2_out, D_3, not_2_out, not_3_out);
  and C_3 (C_3_out, D_3, not_1_out, D_1);
  or or_1 (F, and_1_out, and_2_out, and_3_out, C_1_out, C_2_out, C_3_out);
endmodule
